# Fritzing sketch tarefa_01 (saved by Fritzing 0.9.3b)
breadboards: 1

parts:
  S1 = Pushbutton [package="[THT]"]
  S2 = Pushbutton [package="[THT]"]
  LED1 = LED - 5mm [color="Red (633nm)" package="5 mm [THT]"]
  Componente1 = Arduino Mega ADK (Rev3)
  R2 = Resistor [tolerance=±5% resistance=3.3k package=THT]
  R3 = Resistor [tolerance=±5% resistance=3.3k package=THT]

nets:
  N1: S1.Pin_1, S1.Pin_2, Componente1.D10_PWM, R2.Pin_1
  N2: S1.Pin_3, S1.Pin_4, S2.Pin_3, S2.Pin_4, LED1.cathode, Componente1.GND
  N3: S2.Pin_1, S2.Pin_2, Componente1.D8_PWM, R3.Pin_1
  N4: LED1.anode, Componente1.D7_PWM
  N5: Componente1.5V, R2.Pin_0, R3.Pin_0
